# Fritzing sketch park-assist-subaru (saved by Fritzing 0.9.4)
circuit board: 8.46667cm x 5.64444cm
breadboards: 1

parts:
  U1 = NodeMCU V1.0
  RGB_LED = RGB LED (com. cathode, rgb) [package="5 mm [THT]"]
  R1 = Resistor [tolerance=±5% resistance=470 package=THT]
  R2 = Resistor [tolerance=±5% resistance=470 package=THT]
  R3 = Resistor [tolerance=±5% resistance=470 package=THT]
  S1 = Pushbutton [package="[THT]"]
  R4 = Resistor [tolerance=±5% resistance=10k package=THT]
  HC-SR04_Sensor_1 = HC-SR04 Ultrasonic Distance Sensor
  R5 = Resistor [tolerance=±5% resistance=2k package=THT]
  R6 = Resistor [tolerance=±5% resistance=1k package=THT]
  LED_Strip = ws2812b [package="smd 2812b"]
  R7 = Resistor [tolerance=±5% resistance=470 package=THT]

nets:
  N1: U1.D1, RGB_LED.red_anode, R1.Pin_0, R1.Pin_1
  N2: U1.D2, R2.Pin_0
  N3: U1.D3, R3.Pin_0
  N4: U1.D4, R7.Pin_0
  N5: U1.3V3, S1.Pin_3, S1.Pin_4
  GND: U1.GND, R4.Pin_1, HC-SR04_Sensor_1.ECHO, LED_Strip.VSS
  N6: U1.D5, HC-SR04_Sensor_1.TRIG
  N7: U1.D6, R5.Pin_1, R6.Pin_0
  N8: U1.D7, S1.Pin_1, S1.Pin_2, R4.Pin_0
  VIN: U1.Vin, HC-SR04_Sensor_1.VCC, LED_Strip.VDD
  N9: RGB_LED.common_cathode, R5.Pin_0
  N10: RGB_LED.green_anode, R2.Pin_1
  N11: RGB_LED.blue_anode, R3.Pin_1
  N12: HC-SR04_Sensor_1.GND, R6.Pin_1
  N13: LED_Strip.DIN, R7.Pin_1

notes:
  Using 5v to power HC-SR04. Echo output put into 1k/2k voltage divider to get 3.3v signal. RGB LED strip is add on.
  Momentary switch to trigger distance save to EEPROM(Dinges model) or SPIFFS(Ferguson model).

custom parts:
  NodeMCU V1.0: ESP8266 based NodeMCU
